# Fritzing sketch PCB (saved by Fritzing 0.7.12b)
breadboards: 1

parts:
  Ch8 = Generic female header - 3 pins [package=THT]
  Ch7 = Generic female header - 3 pins [package=THT]
  BAT = Generic female header - 3 pins [package=THT]
  Ch6 = Generic female header - 3 pins [package=THT]
  Ch5 = Generic female header - 3 pins [package=THT]
  Ch4 = Generic female header - 3 pins [package=THT]
  Ch3 = Generic female header - 3 pins [package=THT]
  Ch2 = Generic female header - 3 pins [package=THT]
  Ch1 = Generic female header - 3 pins [package=THT]
  S1 = Toggle Switch [package=THT]
  Arduino1 = Arduino

nets:
  N1: Ch8.pin1, Arduino1.D9
  N2: Ch8.pin2, Ch7.pin2, BAT.pin2, Ch6.pin2, Ch5.pin2, Ch4.pin2, Ch3.pin2, Ch2.pin2, Ch1.pin2, Arduino1.+5V
  GND: Ch8.pin3, Ch7.pin3, BAT.pin3, Ch6.pin3, Ch5.pin3, Ch4.pin3, Ch3.pin3, Ch2.pin3, Ch1.pin3, Arduino1.GND
  N3: Ch7.pin1, S1.L1, Arduino1.D8
  N4: BAT.pin1, S1.COM
  N5: Ch6.pin1, Arduino1.D7
  N6: Ch5.pin1, Arduino1.D6
  N7: Ch4.pin1, Arduino1.D5
  N8: Ch3.pin1, Arduino1.D4
  N9: Ch2.pin1, Arduino1.D3
  N10: Ch1.pin1, Arduino1.D2

notes:
  BAT/PPM
  CHs/PWM
